# Fritzing sketch OD600 (saved by Fritzing 0.9.6b)
breadboards: 1

parts:
  Teensy1 = Teensy 3.1
  Part1 = Adafruit TSL2591 [part_number="Adafruit #1980"]
  LED1 = LED - 5mm [color="Orange (605nm)" current=0.030 package="5 mm [THT]"]
  OLED = Grove OLED 128x96

nets:
  GND: Teensy1.GND, Part1.GND, LED1.cathode, OLED.GND
  N1: Teensy1.A4/D18, Part1.SDA, OLED.SDA
  N2: Teensy1.A5/D19, Part1.SCL, OLED.SCL
  VIN: Part1.VIN, LED1.anode, OLED.VCC

custom parts:
  Teensy 3.1: The Teensy is a complete USB-based microcontoller development system, in a very small footprint, capable of implementing many types of projects. All programming is done via the USB port. No special programmer is needed, only a standard micro-USB cable and a PC or Macintosh with a USB port. It has a USB keyboard/mouse/joystick emulation stack and can be programmed through Arduino IDE.
  Adafruit TSL2591: When the future is dazzlingly-bright, this ultra-high-range luminosity sensor will help you measure it. The TSL2591 luminosity sensor is an advanced digital light sensor, ideal for use in a wide range of light situations. Compared to low cost CdS cells, this sensor is more precise, allowing for exact lux calculations and can be configured for different gain/timing ranges to detect light ranges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
